# Fritzing sketch BATMAN (saved by Fritzing 1.0.2b)
breadboards: 1

parts:
  M1 = gear-motor-encoder-magnet
  M2 = gear-motor-encoder-magnet
  M3 = MH Sensor Series 4-pin IR Sensor/Line follower [package=THT]
  M4 = MH Sensor Series 4-pin IR Sensor/Line follower [package=THT]
  Part1 = Adafruit Proto Shield R3 [part_number="Adafruit #2077"]
  HC-SR04_Sensor_1 = HC-SR04 Ultrasonic Distance Sensor
  BAT1 = 6xAA battery
  S1 = Hall Sensor [part_number=WSH130 package=TO92]  # not connected
  S2 = Hall Sensor [part_number=WSH130 package=TO92]  # not connected
  IC1 = L293D [package=THT]

nets:
  N1: M1.pin_1, Part1.F11, Part1.G11, Part1.J11, IC1.Out_4_(_Controlled_by_Enable_2_)
  N2: M1.pin_2, Part1.F8, Part1.G8, Part1.J8, IC1.Out_3_(_Controlled_by_Enable_2_)
  N3: M2.pin_1, Part1.A8, Part1.E8, IC1.Out_2_(_Controlled_by_Enable_1_)
  N4: M2.pin_2, Part1.A11, Part1.E11, IC1.Out_1_(_Controlled_by_Enable_1_)
  N5: M3.pin2, Part1.D8
  GND: M3.pin3, M4.pin3, Part1.D9, Part1.E9, Part1.E10, Part1.F9, Part1.F10, Part1.G9, Part1.G10, Part1.I10, Part1.GND, HC-SR04_Sensor_1.GND, BAT1.Pin_1, IC1.0V
  +5V: M3.pin4, M4.pin4, Part1.F13, Part1.G13, Part1.H13, Part1.+5V, HC-SR04_Sensor_1.VCC, IC1.+V
  N6: M4.pin2, Part1.D7
  N7: Part1.B7, Part1.E7, Part1.D2, IC1.In_2
  N8: Part1.B12, Part1.E12, Part1.D1, IC1.In_1
  N9: Part1.C6, Part1.E6, Part1.VIN, BAT1.Pin_2, IC1.+Vmotor
  N10: Part1.D13, Part1.E13, Part1.D0, IC1.Enable_1
  N11: Part1.F6, Part1.G6, Part1.J6, Part1.A0, IC1.Enable_2
  N12: Part1.F7, Part1.G7, Part1.I7, Part1.A1, IC1.In_3
  N13: Part1.F12, Part1.G12, Part1.J12, Part1.A2, IC1.In_4
  N14: Part1.D11, HC-SR04_Sensor_1.ECHO
  N15: Part1.D12, HC-SR04_Sensor_1.TRIG

custom parts:
  gear-motor-encoder-magnet: Generic gear motor, 3V to 6V, dual output shafts, 1:48 gear ratio with magnet for wheel encoder
  MH Sensor Series 4-pin IR Sensor/Line follower: modified version of FC-51 from Peter Van Epp (vanepp in forums) This is the 4-pin version of IR line follower module, using the TCRT5000 sensor and LM393 comparator This one has the analogue output pin, in addition to the Digital pin which is set by the trimmer. The Analog pin can feed an Arduino ADC input, for much better level sensing options and less drift than the crappy potentiometer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
  Adafruit Proto Shield R3: This prototyping shield is the best out there (well, we think so, at least), and now is even better with Version R3 - updated for the most compatibility with just about all the Arduinos! It works with UNO, Mega, Leonardo, NG, Diecimila, Duemilanove, and compatible Arduinos. Yun's and Arduino Ethernets have a chunky Ethernet jack that gets in the way of stacking, you can use the stacking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
  Hall Sensor: A Hall Sensor
